# Fritzing sketch circuit (saved by Fritzing 0.9.2b)
breadboards: 1

parts:
  Bauteil1 = Arduino Uno (Rev3)
  Power_plug1 = Power plug
  Q1 = npn-Powertransistor [part_number=TIP120 package="TO220 [THT]"]
  Q2 = npn-Powertransistor [part_number=TIP120 package="TO220 [THT]"]
  Q3 = npn-Powertransistor [part_number=TIP120 package="TO220 [THT]"]
  R1 = Resistor [tolerance=±5% resistance=220 package=THT]
  R2 = Resistor [tolerance=±5% resistance=220 package=THT]
  R3 = Resistor [tolerance=±5% resistance=220 package=THT]
  IR1 = TSOP312.., 314.. [package=THT]

nets:
  N1: Bauteil1.D9_PWM, R1.Pin_0
  N2: Bauteil1.D10_PWM/SS, R2.Pin_0
  N3: Bauteil1.D11_PWM/MOSI, R3.Pin_0
  N4: Bauteil1.D2, IR1.Data
  N5: Bauteil1.3V3, IR1.Vs
  GND: Bauteil1.GND, Power_plug1.GND, Q1.emitter, Q2.emitter, Q3.emitter, IR1.GND
  N6: Q1.base, R1.Pin_1
  N7: Q2.base, R2.Pin_1
  N8: Q3.base, R3.Pin_1

notes:
  12V DC IN
  +12V
  G
  R LED Stripe
  B
